# Fritzing sketch JET ENGINE CKT (saved by Fritzing 0.9.3b)

parts:
  U1 = ESP32-38PinWide [part_number=ESP32-38PinWide]
  L298N1 = L298N DC motor driver
  VCC1 = Battery
  M1 = DC Motor
  DHT1 = DHT11 Humitidy and Temperature Sensor
  Mod1 = KY-026 Flame Sensor Module [package="Breakout board"]
  Sensor1 = Gas Sensor Breakout Board

nets:
  N1: U1.GPIO34, Sensor1.AOUT
  N2: U1.GPIO33, Mod1.A0
  N3: U1.GPIO25, L298N1.IN1
  N4: U1.GPIO26, L298N1.IN2
  N5: U1.GPIO27, DHT1.DATA
  N6: U1.GPIO14, L298N1.ENA
  5V: U1.VIN, L298N1.5V, DHT1.VDD, Mod1.+, Sensor1.5V
  N7: L298N1.OUT1, M1.pin_2
  N8: L298N1.OUT2, M1.pin_1
  N9: L298N1.12V, VCC1.+
  GND: L298N1.GND, VCC1.-, DHT1.GND, Mod1.G, Sensor1.GND

custom parts:
  ESP32-38PinWide: Generic 38-Pin ESP32 with wide format (only access to one side of pins on a breadboard) based on Stephen Lilley's HiLetgo ESP-WROOM-32 ESP32 ESP-32S Development Board.
  L298N DC motor driver: 2x DC motor driver with 78M05 positive voltage regulator (7..35 V) L298N: max 46 V, 2 A Set 5 V Enable jumper to enable 5 V regultor (needed for the L298N) and +5 V output at screw terminal or supply external +5 V at screw terminal Set ENA and/or ENB to +5 V to enable motor permanently or supply ENA and/or ENB with PWM signal IN1 and IN2 set rotation directory for motor A (OUT1/OUT2) IN2 and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
  DHT11 Humitidy and Temperature Sensor: DHT11 Humidity and Temperature Sensor
  KY-026 Flame Sensor Module: KY-026 Flame Sensor Module reacts in the presence of fire.
  Gas Sensor Breakout Board: Gas sensor breakout board. Input voltage is 5V. Sensor output is available in analog and digital.
